# Fritzing sketch CWFA (saved by Fritzing 0.9.2b)
circuit board: 8.46667cm x 5.64444cm

parts:
  Parte1 = Arduino Nano (Rev3.0)
  Parte2 = InvenSense MPU6050
  JP1 = Header 5x2 [package=2x5-ra]
  JP2 = Header 5x2 [package=2x5-ra]
  S2 = Pushbutton [package="[SMD]"]
  R2 = Resistor [tolerance=±5% resistance=330 package=THT]
  JP3 = Header 5x2 [package=2x5-ra]
  S1 = Pushbutton [package="[SMD]"]
  R1 = Resistor [tolerance=±5% resistance=330 package=THT]

nets:
  N1: Parte1.GND, JP1.4, JP2.3
  N2: Parte1.D8, JP2.7
  N3: Parte1.D9, JP2.5
  N4: Parte1.5V, JP2.1
  N5: Parte1.A5, JP1.8
  N6: Parte1.A4, JP1.6
  N7: Parte1.3V3, JP1.2
  N8: Parte2.VCC, JP1.1
  N9: Parte2.GND, JP1.3
  N10: Parte2.SCL, JP1.7
  N11: Parte2.SDA, JP1.5
  N12: JP2.2, JP3.4
  N13: JP2.4, JP3.2
  N14: JP2.6, JP3.8
  N15: JP2.8, JP3.6
  N16: S2.Pin_1, S2.Pin_2, R2.Pin_0, JP3.5
  N17: S2.Pin_3, S2.Pin_4, JP3.3, JP3.7, S1.Pin_1, S1.Pin_2, R1.Pin_0
  N18: R2.Pin_1, JP3.1, R1.Pin_1

// code stored in the sketch: bluetooth_test.ino
void setup(){ 
  delay(500);              // Espera antes de encender el modulo
  Serial1.begin(57600);
}

void loop(){
  bt_connection();
}

//  Conexión Bluetooth
void bt_connection(){
  if(Serial1.available()){
    String socket = Serial1.readStringUntil('\n');
    if(socket == "get_data"){
      Serial1.write("TESTING");
    }
  }
}
