# Fritzing sketch Prototipo (saved by Fritzing 0.9.2b)
circuit board: 8.46667cm x 5.64444cm

parts:
  R1 = Resistor [tolerance=±5% resistance=220 package=THT]
  LED1 = smd LED [color="Red (633nm)" package="1206 [SMD]"]
  Pro_Micro1 = SparkFun Pro Micro
  MPU9250 = MPU 9250 Breakout [package="SIP (Single Inline) [THT]"]
  HC-05 = Bluetooth HC-05 Macho
  VCC1 = 4 x AAA Battery Mount

nets:
  N1: R1.Pin_0, LED1.cathode
  GND: R1.Pin_1, Pro_Micro1.GND, MPU9250.GND, HC-05.GND, VCC1.-
  N2: LED1.anode, Pro_Micro1.5
  N3: Pro_Micro1.TX0, HC-05.RXD
  N4: Pro_Micro1.RX1, HC-05.TXD
  N5: Pro_Micro1.2, MPU9250.SDA
  N6: Pro_Micro1.3, MPU9250.SCL
  VCC: MPU9250.VCC, HC-05.VCC, VCC1.+

custom parts:
  SparkFun Pro Micro: The Pro Micro is similar to the Pro Mini except with an ATmega32U4 on board. The USB transceiver inside the 32U4 allows us to add USB connectivity on-board and do away with bulky external USB interface. Based on: https://github.com/unorthodox-engineers/unorthodox-arduino/blob/master/Unorthodox/fritzing/parts/Pro%20Micro.fzpz
  MPU 9250 Breakout: Generic MPU 9250 Breakout Board

// code stored in the sketch: bluetooth_test.ino
void setup(){ 
  delay(500);              // Espera antes de encender el modulo
  Serial1.begin(57600);
}

void loop(){
  bt_connection();
}

//  Conexión Bluetooth
void bt_connection(){
  if(Serial1.available()){
    String socket = Serial1.readStringUntil('\n');
    if(socket == "get_data"){
      Serial1.write("TESTING");
    }
  }
}
